// Logisim project main.circ as structural Verilog: 6 circuits, main circuit main
module main (
  input  [4:0] in_1,
  input  [1:0] in_2
);

  wire clock_1_out;
  wire [31:0] dispalycontroller_1_out_5, dispalycontroller_1_out_6, dispalycontroller_1_out_7,
       dispalycontroller_1_out_8, dispalycontroller_1_out_9, dispalycontroller_1_out_10,
       dispalycontroller_1_out_11, dispalycontroller_1_out_12, dispalycontroller_1_out_13,
       dispalycontroller_1_out_14, dispalycontroller_1_out_15, dispalycontroller_1_out_16,
       dispalycontroller_1_out_17, dispalycontroller_1_out_18, dispalycontroller_1_out_19,
       dispalycontroller_1_out_20, dispalycontroller_1_out_21, dispalycontroller_1_out_22,
       dispalycontroller_1_out_23, dispalycontroller_1_out_24, dispalycontroller_1_out_25,
       dispalycontroller_1_out_26, dispalycontroller_1_out_27, dispalycontroller_1_out_28,
       dispalycontroller_1_out_29, dispalycontroller_1_out_30, dispalycontroller_1_out_31,
       dispalycontroller_1_out_32, dispalycontroller_1_out_33, dispalycontroller_1_out_34,
       dispalycontroller_1_out_35, dispalycontroller_1_out_36, drawtank_1_line_1, drawtank_1_line_2,
       drawtank_1_line_3;

  DotMatrix #(.matrixrows(32)) dotmatrix_1 (
    .col0({32{1'b0}}), .col1(drawtank_1_line_1), .col2(drawtank_1_line_2), .col3(drawtank_1_line_3),
    .col4({32{1'b0}}));
  drawTank drawtank_1 (
    .Y(in_1), .Way(in_2), .line_1(drawtank_1_line_1), .line_2(drawtank_1_line_2), .line_3(drawtank_1_line_3));
  tankObjectPlayer tankobjectplayer_1 ();  // open: clock, isShot, isDrive, Reset, way, X_output, out_7, out_8, out_9
  Clock clock_1 (.out(clock_1_out));
  DotMatrix #(.matrixcols(32), .matrixrows(32)) dotmatrix_2 (
    .col0(dispalycontroller_1_out_5), .col1(dispalycontroller_1_out_6), .col2(dispalycontroller_1_out_7),
    .col3(dispalycontroller_1_out_8), .col4(dispalycontroller_1_out_9), .col5(dispalycontroller_1_out_10),
    .col6(dispalycontroller_1_out_11), .col7(dispalycontroller_1_out_12), .col8(dispalycontroller_1_out_13),
    .col9(dispalycontroller_1_out_14), .col10(dispalycontroller_1_out_15),
    .col11(dispalycontroller_1_out_16), .col12(dispalycontroller_1_out_17),
    .col13(dispalycontroller_1_out_18), .col14(dispalycontroller_1_out_19),
    .col15(dispalycontroller_1_out_20), .col16(dispalycontroller_1_out_21),
    .col17(dispalycontroller_1_out_22), .col18(dispalycontroller_1_out_23),
    .col19(dispalycontroller_1_out_24), .col20(dispalycontroller_1_out_25),
    .col21(dispalycontroller_1_out_26), .col22(dispalycontroller_1_out_27),
    .col23(dispalycontroller_1_out_28), .col24(dispalycontroller_1_out_29),
    .col25(dispalycontroller_1_out_30), .col26(dispalycontroller_1_out_31),
    .col27(dispalycontroller_1_out_32), .col28(dispalycontroller_1_out_33),
    .col29(dispalycontroller_1_out_34), .col30(dispalycontroller_1_out_35), .col31(dispalycontroller_1_out_36));
  dispalyController dispalycontroller_1 (
    .out_5(dispalycontroller_1_out_5), .out_17(dispalycontroller_1_out_17),
    .out_29(dispalycontroller_1_out_29), .out_6(dispalycontroller_1_out_6),
    .out_18(dispalycontroller_1_out_18), .out_30(dispalycontroller_1_out_30),
    .out_7(dispalycontroller_1_out_7), .out_19(dispalycontroller_1_out_19),
    .out_31(dispalycontroller_1_out_31), .out_8(dispalycontroller_1_out_8),
    .out_20(dispalycontroller_1_out_20), .out_32(dispalycontroller_1_out_32),
    .out_9(dispalycontroller_1_out_9), .out_21(dispalycontroller_1_out_21),
    .out_33(dispalycontroller_1_out_33), .out_10(dispalycontroller_1_out_10),
    .out_22(dispalycontroller_1_out_22), .out_34(dispalycontroller_1_out_34),
    .out_11(dispalycontroller_1_out_11), .out_23(dispalycontroller_1_out_23),
    .out_35(dispalycontroller_1_out_35), .out_12(dispalycontroller_1_out_12),
    .out_24(dispalycontroller_1_out_24), .out_36(dispalycontroller_1_out_36),
    .out_13(dispalycontroller_1_out_13), .out_25(dispalycontroller_1_out_25),
    .out_14(dispalycontroller_1_out_14), .out_26(dispalycontroller_1_out_26),
    .out_15(dispalycontroller_1_out_15), .out_27(dispalycontroller_1_out_27),
    .out_16(dispalycontroller_1_out_16), .out_28(dispalycontroller_1_out_28));  // open: clock, column, picture, selectCol
  Button button ();  // open: out
  Button button_2 ();  // open: out
  Button button_3 ();  // open: out
  Button button_4 ();  // open: out
endmodule

module dispalyController (
  input  clock,
  input  [4:0] column,
  input  [31:0] picture,
  output [31:0] selectCol,
  output [31:0] out_5,
  output [31:0] out_6,
  output [31:0] out_7,
  output [31:0] out_8,
  output [31:0] out_9,
  output [31:0] out_10,
  output [31:0] out_11,
  output [31:0] out_12,
  output [31:0] out_13,
  output [31:0] out_14,
  output [31:0] out_15,
  output [31:0] out_16,
  output [31:0] out_17,
  output [31:0] out_18,
  output [31:0] out_19,
  output [31:0] out_20,
  output [31:0] out_21,
  output [31:0] out_22,
  output [31:0] out_23,
  output [31:0] out_24,
  output [31:0] out_25,
  output [31:0] out_26,
  output [31:0] out_27,
  output [31:0] out_28,
  output [31:0] out_29,
  output [31:0] out_30,
  output [31:0] out_31,
  output [31:0] out_32,
  output [31:0] out_33,
  output [31:0] out_34,
  output [31:0] out_35,
  output [31:0] out_36
);

  wire [31:0] s0, s1, s2, s3, s4, s5, s6, s7, s8, s9, s10, s11, s12, s13, s14, s15, s16, s17, s18, s19, s20,
       s21, s22, s23, s24, s25, s26, s27, s28, s29, s30, s31;

  Register #(.width(32), .trigger("falling")) register_1 (.D(s0), .Q(out_5), .clk(clock));  // open: en, clr
  Register #(.width(32), .trigger("falling")) register_2 (.D(s12), .Q(out_17), .clk(clock));  // open: en, clr
  Register #(.width(32), .trigger("falling")) register_3 (.D(s24), .Q(out_29), .clk(clock));  // open: en, clr
  Register #(.width(32), .trigger("falling")) register_4 (.D(s1), .Q(out_6), .clk(clock));  // open: en, clr
  Register #(.width(32), .trigger("falling")) register_5 (.D(s13), .Q(out_18), .clk(clock));  // open: en, clr
  Register #(.width(32), .trigger("falling")) register_6 (.D(s25), .Q(out_30), .clk(clock));  // open: en, clr
  Register #(.width(32), .trigger("falling")) register_7 (.D(s2), .Q(out_7), .clk(clock));  // open: en, clr
  Register #(.width(32), .trigger("falling")) register_8 (.D(s14), .Q(out_19), .clk(clock));  // open: en, clr
  Register #(.width(32), .trigger("falling")) register_9 (.D(s26), .Q(out_31), .clk(clock));  // open: en, clr
  Demultiplexer #(.select(5), .width(32), .enable("false")) demultiplexer_1 (
    .out0(s0), .out1(s1), .out2(s2), .out3(s3), .out4(s4), .out5(s5), .out6(s6), .out7(s7), .out8(s8),
    .out9(s9), .out10(s10), .out11(s11), .out12(s12), .out13(s13), .out14(s14), .out15(s15), .out16(s16),
    .out17(s17), .out18(s18), .out19(s19), .out20(s20), .out21(s21), .out22(s22), .out23(s23), .out24(s24),
    .out25(s25), .out26(s26), .out27(s27), .out28(s28), .out29(s29), .out30(s30), .out31(s31), .in(picture),
    .sel(column));
  Register #(.width(32), .trigger("falling")) register_10 (.D(s3), .Q(out_8), .clk(clock));  // open: en, clr
  Register #(.width(32), .trigger("falling")) register_11 (.D(s15), .Q(out_20), .clk(clock));  // open: en, clr
  Register #(.width(32), .trigger("falling")) register_12 (.D(s27), .Q(out_32), .clk(clock));  // open: en, clr
  Register #(.width(32), .trigger("falling")) register_13 (.D(s4), .Q(out_9), .clk(clock));  // open: en, clr
  Register #(.width(32), .trigger("falling")) register_14 (.D(s16), .Q(out_21), .clk(clock));  // open: en, clr
  Register #(.width(32), .trigger("falling")) register_15 (.D(s28), .Q(out_33), .clk(clock));  // open: en, clr
  Register #(.width(32), .trigger("falling")) register_16 (.D(s5), .Q(out_10), .clk(clock));  // open: en, clr
  Register #(.width(32), .trigger("falling")) register_17 (.D(s17), .Q(out_22), .clk(clock));  // open: en, clr
  Register #(.width(32), .trigger("falling")) register_18 (.D(s29), .Q(out_34));  // open: en, clk, clr
  Register #(.width(32), .trigger("falling")) register_19 (.D(s6), .Q(out_11), .clk(clock));  // open: en, clr
  Register #(.width(32), .trigger("falling")) register_20 (.D(s18), .Q(out_23), .clk(clock));  // open: en, clr
  Register #(.width(32), .trigger("falling")) register_21 (.D(s30), .Q(out_35), .clk(clock));  // open: en, clr
  Register #(.width(32), .trigger("falling")) register_22 (.D(s7), .Q(out_12), .clk(clock));  // open: en, clr
  Register #(.width(32), .trigger("falling")) register_23 (.D(s19), .Q(out_24), .clk(clock));  // open: en, clr
  Register #(.width(32), .trigger("falling")) register_24 (.D(s31), .Q(out_36), .clk(clock));  // open: en, clr
  Register #(.width(32), .trigger("falling")) register_25 (.D(s8), .Q(out_13), .clk(clock));  // open: en, clr
  Register #(.width(32), .trigger("falling")) register_26 (.D(s20), .Q(out_25), .clk(clock));  // open: en, clr
  Register #(.width(32), .trigger("falling")) register_27 (.D(s9), .Q(out_14), .clk(clock));  // open: en, clr
  Register #(.width(32), .trigger("falling")) register_28 (.D(s21), .Q(out_26));  // open: en, clk, clr
  Register #(.width(32), .trigger("falling")) register_29 (.D(s10), .Q(out_15), .clk(clock));  // open: en, clr
  Register #(.width(32), .trigger("falling")) register_30 (.D(s22), .Q(out_27), .clk(clock));  // open: en, clr
  Multiplexer #(.select(5), .width(32), .enable("false")) multiplexer_1 (
    .in0(out_5), .in1(out_6), .in2(out_7), .in3(out_8), .in4(out_9), .in5(out_10), .in6(out_11),
    .in7(out_12), .in8(out_13), .in9(out_14), .in10(out_15), .in11(out_16), .in12(out_17), .in13(out_18),
    .in14(out_19), .in15(out_20), .in16(out_21), .in17(out_22), .in18(out_23), .in19(out_24), .in20(out_25),
    .in21(out_26), .in22(out_27), .in23(out_28), .in24(out_29), .in25(out_30), .in26(out_31), .in27(out_32),
    .in28(out_33), .in29(out_34), .in30(out_35), .in31(out_36), .out(selectCol), .sel(column));
  Register #(.width(32), .trigger("falling")) register_31 (.D(s11), .Q(out_16), .clk(clock));  // open: en, clr
  Register #(.width(32), .trigger("falling")) register_32 (.D(s23), .Q(out_28), .clk(clock));  // open: en, clr

  // Other names for the same wires on the sheet: clk = clock; col[4:0] = column; o0[31:0] = out_5; o1[31:0] = out_6;
  //   o2[31:0] = out_7; o3[31:0] = out_8; o4[31:0] = out_9; o5[31:0] = out_10; o6[31:0] = out_11; o7[31:0] = out_12;
  //   o8[31:0] = out_13; o9[31:0] = out_14; o10[31:0] = out_15; o11[31:0] = out_16; o12[31:0] = out_17;
  //   o13[31:0] = out_18; o14[31:0] = out_19; o15[31:0] = out_20; o16[31:0] = out_21; o17[31:0] = out_22;
  //   o18[31:0] = out_23; o19[31:0] = out_24; o20[31:0] = out_25; o21[31:0] = out_26; o22[31:0] = out_27;
  //   o23[31:0] = out_28; o24[31:0] = out_29; o25[31:0] = out_30; o26[31:0] = out_31; o27[31:0] = out_32;
  //   o28[31:0] = out_33; o29[31:0] = out_34; o30[31:0] = out_35; o31[31:0] = out_36
endmodule

module tankObjectPlayer (
  input  clock,
  input  isShot,
  input  isDrive,
  input  Reset,
  input  [1:0] way,
  output [4:0] X_output,
  output [31:0] out_7,
  output [31:0] out_8,
  output [31:0] out_9
);

  wire comparator_1_eq, comparator_2_eq, comparator_3_eq, comparator_4_eq;
  wire [1:0] dirTank;
  wire [4:0] dec5_1_out, dec5_2_out, inc5_1_out, inc5_2_out, multiplexer_1_out, multiplexer_2_out,
       multiplexer_3_out, multiplexer_4_out, multiplexer_5_out, multiplexer_6_out, multiplexer_7_out,
       multiplexer_8_out, y_cord_tank;

  Comparator #(.width(5), .mode("unsigned")) comparator_1 (
    .a(5'b11110), .b(X_output), .eq(comparator_1_eq));  // open: gt, lt
  inc5 inc5_1 (.in(X_output), .out(inc5_1_out));
  Multiplexer #(.width(5), .enable("false")) multiplexer_1 (
    .in0(inc5_1_out), .in1(X_output), .out(multiplexer_1_out), .sel(comparator_1_eq));
  Register #(.width(2), .trigger("falling")) DirectionTank (.D(way), .Q(dirTank), .clk(clock));  // open: en, clr
  Comparator #(.width(5), .mode("unsigned")) comparator_2 (
    .a(5'b00001), .b(X_output), .eq(comparator_2_eq));  // open: gt, lt
  dec5 dec5_1 (.in(X_output), .out(dec5_1_out));
  Multiplexer #(.width(5), .enable("false")) multiplexer_2 (
    .in0(dec5_1_out), .in1(X_output), .out(multiplexer_2_out), .sel(comparator_2_eq));
  Multiplexer #(.select(2), .width(5), .enable("false")) multiplexer_3 (
    .in0(multiplexer_2_out), .in1(X_output), .in2(multiplexer_1_out), .in3(X_output),
    .out(multiplexer_3_out), .sel(dirTank));
  Multiplexer #(.width(5), .enable("false")) multiplexer_4 (
    .in0(multiplexer_3_out), .in1(5'b00001), .out(multiplexer_4_out), .sel(Reset));
  Register #(.width(5), .trigger("falling")) xTank (
    .D(multiplexer_4_out), .en(isDrive), .Q(X_output), .clk(clock));  // open: clr
  Register #(.width(5), .trigger("falling")) xBullet ();  // open: D, en, Q, clk, clr
  Register #(.width(5), .trigger("falling")) yBullet ();  // open: D, en, Q, clk, clr
  Register #(.width(2), .trigger("falling")) DirectionBullet ();  // open: D, en, Q, clk, clr
  Comparator #(.width(5), .mode("unsigned")) comparator_3 (
    .a(5'b11110), .b(y_cord_tank), .eq(comparator_3_eq));  // open: gt, lt
  inc5 inc5_2 (.in(y_cord_tank), .out(inc5_2_out));
  Multiplexer #(.width(5), .enable("false")) multiplexer_5 (
    .in0(inc5_2_out), .in1(y_cord_tank), .out(multiplexer_5_out), .sel(comparator_3_eq));
  Comparator #(.width(5), .mode("unsigned")) comparator_4 (
    .a(5'b00001), .b(y_cord_tank), .eq(comparator_4_eq));  // open: gt, lt
  dec5 dec5_2 (.in(y_cord_tank), .out(dec5_2_out));
  Multiplexer #(.width(5), .enable("false")) multiplexer_6 (
    .in0(dec5_2_out), .in1(y_cord_tank), .out(multiplexer_6_out), .sel(comparator_4_eq));
  Multiplexer #(.select(2), .width(5), .enable("false")) multiplexer_7 (
    .in0(y_cord_tank), .in1(multiplexer_5_out), .in2(y_cord_tank), .in3(multiplexer_6_out),
    .out(multiplexer_7_out), .sel(dirTank));
  Multiplexer #(.width(5), .enable("false")) multiplexer_8 (
    .in0(multiplexer_7_out), .in1(5'b00001), .out(multiplexer_8_out), .sel(Reset));
  drawTank drawtank_1 (.Y(y_cord_tank), .Way(dirTank), .line_1(out_7), .line_2(out_8), .line_3(out_9));
  Register #(.width(5), .trigger("falling")) yTank (
    .D(multiplexer_8_out), .en(isDrive), .Q(y_cord_tank), .clk(clock));  // open: clr

  // Other names for the same wires on the sheet: clk = clock; drive = isDrive; x_cord_tank[4:0] = X_output
endmodule

module drawTank (
  input  [4:0] Y,
  input  [1:0] Way,
  output [31:0] line_1,
  output [31:0] line_2,
  output [31:0] line_3
);

  wire [4:0] dec5_1_out, dec5_2_out, dec5_3_out, dec5_4_out, dec5_5_out, inc5_1_out, inc5_2_out, inc5_3_out,
       inc5_4_out, inc5_5_out;
  wire [31:0] down_Line_1, down_Line_2, down_Line_3, left_Line_1, left_Line_2, left_Line_3, shifter_1_out,
       shifter_2_out, shifter_3_out, shifter_4_out, shifter_5_out, shifter_7_out, shifter_8_out,
       shifter_9_out, shifter_10_out, shifter_11_out, shifter_12_out, shifter_13_out, shifter_14_out,
       shifter_15_out, shifter_16_out, shifter_17_out, shifter_18_out, up_Line_1, up_Line_2, up_Line_3;

  Shifter #(.width(32)) shifter_1 (.in(32'h1), .\dist (dec5_1_out), .out(shifter_1_out));
  dec5 dec5_1 (.in(Y), .out(dec5_1_out));
  Shifter #(.width(32)) shifter_2 (.in(32'h1), .\dist (Y), .out(shifter_2_out));
  Shifter #(.width(32)) shifter_3 (.in(32'h1), .\dist (inc5_1_out), .out(shifter_3_out));
  inc5 inc5_1 (.in(Y), .out(inc5_1_out));
  Shifter #(.width(32)) shifter_4 (.in(32'h1), .\dist (dec5_2_out), .out(shifter_4_out));
  dec5 dec5_2 (.in(Y), .out(dec5_2_out));
  Shifter #(.width(32)) shifter_5 (.in(32'h1), .\dist (inc5_2_out), .out(shifter_5_out));
  inc5 inc5_2 (.in(Y), .out(inc5_2_out));
  Shifter #(.width(32)) shifter_6 (.in(32'h1), .\dist (Y), .out(left_Line_1));
  assign left_Line_2 = shifter_1_out | shifter_2_out | shifter_3_out;  // OR_Gate or_1, 32 bits wide
  assign left_Line_3 = shifter_4_out | shifter_5_out;  // OR_Gate or_2, 32 bits wide
  Shifter #(.width(32)) shifter_7 (.in(32'h1), .\dist (dec5_3_out), .out(shifter_7_out));
  dec5 dec5_3 (.in(Y), .out(dec5_3_out));
  Shifter #(.width(32)) shifter_8 (.in(32'h1), .\dist (Y), .out(shifter_8_out));
  Shifter #(.width(32)) shifter_9 (.in(32'h1), .\dist (inc5_3_out), .out(shifter_9_out));
  inc5 inc5_3 (.in(Y), .out(inc5_3_out));
  Shifter #(.width(32)) shifter_10 (.in(32'h1), .\dist (Y), .out(shifter_10_out));
  Shifter #(.width(32)) shifter_11 (.in(32'h1), .\dist (dec5_4_out), .out(shifter_11_out));
  dec5 dec5_4 (.in(Y), .out(dec5_4_out));
  Shifter #(.width(32)) shifter_12 (.in(32'h1), .\dist (Y), .out(shifter_12_out));
  assign up_Line_1 = shifter_7_out | shifter_8_out;  // OR_Gate or_3, 32 bits wide
  assign up_Line_2 = shifter_9_out | shifter_10_out;  // OR_Gate or_4, 32 bits wide
  assign up_Line_3 = shifter_11_out | shifter_12_out;  // OR_Gate or_5, 32 bits wide
  Multiplexer #(.select(2), .width(32), .enable("false")) multiplexer_1 (
    .in0(left_Line_1), .in1(up_Line_1), .in2(left_Line_3), .in3(down_Line_1), .out(line_1), .sel(Way));
  Multiplexer #(.select(2), .width(32), .enable("false")) multiplexer_2 (
    .in0(left_Line_2), .in1(up_Line_2), .in2(left_Line_2), .in3(down_Line_2), .out(line_2), .sel(Way));
  Multiplexer #(.select(2), .width(32), .enable("false")) multiplexer_3 (
    .in0(left_Line_3), .in1(up_Line_3), .in2(left_Line_1), .in3(down_Line_3), .out(line_3), .sel(Way));
  Shifter #(.width(32)) shifter_13 (.in(32'h1), .\dist (inc5_4_out), .out(shifter_13_out));
  inc5 inc5_4 (.in(Y), .out(inc5_4_out));
  Shifter #(.width(32)) shifter_14 (.in(32'h1), .\dist (Y), .out(shifter_14_out));
  Shifter #(.width(32)) shifter_15 (.in(32'h1), .\dist (dec5_5_out), .out(shifter_15_out));
  dec5 dec5_5 (.in(Y), .out(dec5_5_out));
  Shifter #(.width(32)) shifter_16 (.in(32'h1), .\dist (Y), .out(shifter_16_out));
  Shifter #(.width(32)) shifter_17 (.in(32'h1), .\dist (inc5_5_out), .out(shifter_17_out));
  inc5 inc5_5 (.in(Y), .out(inc5_5_out));
  Shifter #(.width(32)) shifter_18 (.in(32'h1), .\dist (Y), .out(shifter_18_out));
  assign down_Line_1 = shifter_13_out | shifter_14_out;  // OR_Gate or_6, 32 bits wide
  assign down_Line_2 = shifter_15_out | shifter_16_out;  // OR_Gate or_7, 32 bits wide
  assign down_Line_3 = shifter_17_out | shifter_18_out;  // OR_Gate or_8, 32 bits wide

  // Notes on the sheet:
  //   00 - влево, 01 - вверх, 10 - вправо, 11 - вниз
endmodule

module inc5 (
  input  [4:0] in,
  output [4:0] out
);

  Adder #(.width(5)) adder_1 (.a(in), .b(5'b00001), .out(out));  // open: cin, cout
endmodule

module dec5 (
  input  [4:0] in,
  output [4:0] out
);

  Subtractor #(.width(5)) subtractor_1 (.a(in), .b(5'b00001), .out(out));  // open: bin, bout
endmodule
